# Fritzing sketch Infrared (saved by Fritzing 0.9.3b)

parts:
  U1 = ESP8266 NodeMCU LoLin module
  LED2 = LED - 5mm [color="Red (633nm)" package="5 mm [THT]"]
  LED3 = LED - 5mm [color="Red (633nm)" package="5 mm [THT]"]
  M1 = fc-51 [package=THT]

nets:
  N1: U1.D0, LED3.anode
  N2: U1.D1, LED2.anode
  N3: U1.D2, M1.pin1
  N4: U1.Vin, M1.pin3
  N5: U1.GND, LED2.cathode, LED3.cathode, M1.pin2

custom parts:
  ESP8266 NodeMCU LoLin module: ESP8266 based NodeMCU
