# Fritzing sketch Photointerrupt (saved by Fritzing 0.9.3b)

parts:
  U1 = ESP8266 NodeMCU LoLin module
  LED2 = LED - 5mm [color="Red (633nm)" package="5 mm [THT]"]
  LED3 = LED - 5mm [color="Red (633nm)" package="5 mm [THT]"]
  Mod1 = KY-010 Photo Interrupter Module [package="Breakout board"]

nets:
  N1: U1.D0, LED3.anode
  N2: U1.D1, LED2.anode
  N3: U1.D2, Mod1.S
  VIN: U1.Vin, Mod1.Vin
  N4: U1.GND, LED2.cathode, LED3.cathode, Mod1.-

custom parts:
  ESP8266 NodeMCU LoLin module: ESP8266 based NodeMCU
  KY-010 Photo Interrupter Module: KY-010 Photo Interrupter Module, it will trigger a signal when light between the sensor's gap is blocked.
