# Fritzing sketch Ultrasoon (saved by Fritzing 0.9.3b)

parts:
  U1 = ESP8266 NodeMCU LoLin module
  LED2 = LED - 5mm [color="Red (633nm)" package="5 mm [THT]"]
  LED3 = LED - 5mm [color="Red (633nm)" package="5 mm [THT]"]
  Part1 = SRF05 Ultrasonic Rangefinder

nets:
  N1: U1.D0, LED3.anode
  N2: U1.D1, LED2.anode
  N3: U1.D2, Part1.Trig
  N4: U1.D3, Part1.Echo
  VIN: U1.Vin, Part1.VCC
  GND: U1.GND, LED2.cathode, LED3.cathode, Part1.GND

custom parts:
  ESP8266 NodeMCU LoLin module: ESP8266 based NodeMCU
