# Fritzing sketch schemaV1 (saved by Fritzing 0.9.3b)

parts:
  part = LCM1602 IIC [part_number="LCM1602 IIC" chip_label="LCM1602 IIC" package="DIP (Dual Inline) [THT]"]
  U1 = LCD-16X2 [package=lcd-16x2]
  Part1 = Arduino Uno (Rev3) - ICSP
  U2 = LIPO-1000mAh [package=lipo-1000]
  R2 = Resistor [tolerance=±5% resistance=220 package="2010 [SMD]"]
  R1 = Resistor [tolerance=±5% resistance=220 package="2010 [SMD]"]

nets:
  VSS: part.VSS, U1.VSS
  VDD: part.VDD, U1.VDD
  N1: part.V0, U1.VO
  N2: part.RS, U1.RS
  N3: part.RW, U1.R_W
  N4: part.E, U1.E
  N5: part.D0, U1.DB0
  N6: part.D1, U1.DB1
  N7: part.D2, U1.DB2
  N8: part.D3, U1.DB3
  N9: part.D4, U1.DB4
  N10: part.D5, U1.DB5
  N11: part.D6, U1.DB6
  N12: part.D7, U1.DB7
  N13: part.A, U1.A
  N14: part.K, U1.K
  GND: part.GND, Part1.GND, U2.+, R2.Pin_0
  VCC: part.VCC, Part1.5V
  N15: part.SDA, Part1.A4/SDA
  N16: part.SCL, Part1.A5/SCL
  N17: part.LED_A, part.LED_B
  N18: Part1.A0, R2.Pin_1, R1.Pin_1
  N19: Part1.VIN, U2.-, R1.Pin_0

custom parts:
  LCM1602 IIC: I2C-Module to use a 1602 or 2004 LCD on with the wire.h libory Serial LCD Modul
