# Fritzing sketch schemaV1 (saved by Fritzing 0.9.3b)

parts:
  LCM1602_IIC1 = LCM1602 IIC [part_number="LCM1602 IIC" chip_label="LCM1602 IIC" package="DIP (Dual Inline) [THT]"]
  U1 = LCD-16X2 [package=lcd-16x2]
  Part1 = Arduino Uno (Rev3) - ICSP
  U2 = LIPO-1000mAh [package=lipo-1000]
  R2 = Resistor [tolerance=±5% resistance=220 package="2010 [SMD]"]
  R1 = Resistor [tolerance=±5% resistance=220 package="2010 [SMD]"]
  LED1 = smd LED [color="Red (633nm)" package="0805 [SMD]"]
  R3 = Resistor [tolerance=±5% resistance=220 package="0805 [SMD]"]
  JP1 = USB_MICROB_PLUG [package=micro-b-th]

nets:
  VSS: LCM1602_IIC1.VSS, U1.VSS
  VDD: LCM1602_IIC1.VDD, U1.VDD
  N1: LCM1602_IIC1.V0, U1.VO
  N2: LCM1602_IIC1.RS, U1.RS
  N3: LCM1602_IIC1.RW, U1.R_W
  N4: LCM1602_IIC1.E, U1.E
  N5: LCM1602_IIC1.D0, U1.DB0
  N6: LCM1602_IIC1.D1, U1.DB1
  N7: LCM1602_IIC1.D2, U1.DB2
  N8: LCM1602_IIC1.D3, U1.DB3
  N9: LCM1602_IIC1.D4, U1.DB4
  N10: LCM1602_IIC1.D5, U1.DB5
  N11: LCM1602_IIC1.D6, U1.DB6
  N12: LCM1602_IIC1.D7, U1.DB7
  N13: LCM1602_IIC1.A, U1.A
  N14: LCM1602_IIC1.K, U1.K
  GND: LCM1602_IIC1.GND, Part1.GND, U2.+, R2.Pin_0, LED1.anode, JP1.GND
  VCC: LCM1602_IIC1.VCC, Part1.5V
  N15: LCM1602_IIC1.SDA, Part1.A4/SDA
  N16: LCM1602_IIC1.SCL, Part1.A5/SCL
  N17: LCM1602_IIC1.LED_A, LCM1602_IIC1.LED_B
  N18: Part1.A0, R2.Pin_1, R1.Pin_1
  N19: Part1.D2, R3.Pin_0, JP1.VCC
  N20: U2.-, R1.Pin_0
  N21: LED1.cathode, R3.Pin_1

custom parts:
  LCM1602 IIC: I2C-Module to use a 1602 or 2004 LCD on with the wire.h libory Serial LCD Modul
