# Fritzing sketch Piezo (saved by Fritzing 0.9.3b)

parts:
  U1 = ESP8266 NodeMCU LoLin module
  J1 = Piezo Speaker
  LED1 = RGB LED (com. cathode, rbg) [package="5 mm [THT]"]
  R1 = Resistor [tolerance=±5% resistance=220 package="0402 [SMD]"]
  LED2 = LED - 5mm [color="Red (633nm)" package="5 mm [THT]"]
  LED3 = LED - 5mm [color="Red (633nm)" package="5 mm [THT]"]

nets:
  N1: U1.D0, LED3.anode
  N2: U1.D1, LED2.anode
  N3: U1.D2, R1.Pin_0
  N4: U1.D3, LED1.red_anode
  N5: U1.D4, LED1.blue_anode
  N6: U1.D5, LED1.green_anode
  N7: U1.Vin, LED1.common_cathode
  N8: U1.GND, J1.pin1, LED2.cathode, LED3.cathode

custom parts:
  ESP8266 NodeMCU LoLin module: ESP8266 based NodeMCU
