# Fritzing sketch Servo (saved by Fritzing 0.9.3b)

parts:
  J1 = Basic Servo
  J2 = Basic Servo
  U1 = ESP8266 NodeMCU LoLin module
  LED1 = LED - 5mm [color="Red (633nm)" package="5 mm [THT]"]
  LED2 = LED - 5mm [color="Red (633nm)" package="5 mm [THT]"]

nets:
  GND: J1.gnd, J2.gnd, U1.GND, LED1.cathode, LED2.cathode
  VCC: J1.vcc, J2.vcc, U1.Vin
  N1: J1.pulse, U1.D3
  N2: J2.pulse, U1.D2
  N3: U1.D0, LED2.anode
  N4: U1.D1, LED1.anode

custom parts:
  ESP8266 NodeMCU LoLin module: ESP8266 based NodeMCU
