# Fritzing sketch schemaV1 (saved by Fritzing 0.9.3b)

parts:
  U1 = NodeMCU V1.0  # not connected
  U2 = NodeMCU V1.0  # not connected
  U3 = NodeMCU V1.0  # not connected
  U4 = NodeMCU V1.0  # not connected
  U5 = NodeMCU V1.0  # not connected
  U6 = NodeMCU V1.0  # not connected
  U7 = NodeMCU V1.0
  VCC1 = Battery block 9V

nets:
  N1: U7.GND, VCC1.-
  N2: U7.Vin, VCC1.+

custom parts:
  NodeMCU V1.0: ESP8266 based NodeMCU
